# Fritzing sketch TCS_230_f (saved by Fritzing 0.9.3b)
breadboards: 1

parts:
  Part1 = Arduino Uno (Rev3)
  LED1 = RGB LED (com. cathode, rgb) [package="5 mm [THT]"]
  e-radionica1 = prefix101209 [part_number=101209]
  R1 = Resistor [tolerance=±5% resistance=220 package=THT]
  R2 = Resistor [tolerance=±5% resistance=220 package=THT]
  R3 = Resistor [tolerance=±5% resistance=220 package=THT]

nets:
  N1: Part1.D8, e-radionica1.connector4
  N2: Part1.D10_PWM/SS, e-radionica1.connector5
  N3: Part1.D11_PWM/MOSI, e-radionica1.connector6
  N4: Part1.D12/MISO, e-radionica1.connector7
  N5: Part1.GND, LED1.common_cathode, e-radionica1.connector1, e-radionica1.connector2
  N6: Part1.D2, R1.Pin_1
  N7: Part1.D3_PWM, R2.Pin_1
  N8: Part1.D4, R3.Pin_1
  N9: Part1.5V, e-radionica1.connector8
  N10: LED1.red_anode, R1.Pin_0
  N11: LED1.green_anode, R2.Pin_0
  N12: LED1.blue_anode, R3.Pin_0
