# Fritzing sketch TCS_230_f (saved by Fritzing 0.9.3b)
breadboards: 1

parts:
  Part1 = Arduino Uno (Rev3)
  LED1 = RGB LED (com. cathode, rgb) [package="5 mm [THT]"]  # not connected
  e-radionica1 = TCS230 Color Sensor [part_number=101209]

nets:
  5V: Part1.5V, e-radionica1.Vcc

custom parts:
  TCS230 Color Sensor: TCS230
